# Fritzing sketch Prototype (saved by Fritzing 0.9.3b)
stripboards: 1

parts:
  IC2 = V_REG_LD1117VXX [package=78xxl]
  U1 = ESP8266 WiFi Module [part_number=ESP8266]
  R1 = PHOTOCELL [package=photocell-kit]
  R2 = Resistor [tolerance=±5% resistance=22k package="0603 [SMD]"]
  T1 = LM335 Temperature Sensor [package="TO92 [THT]"]
  IC1 = DIP - 16 pins [chip_label=PCF8591 package="DIP (Dual Inline) [THT]"]
  C3 = Electrolytic Capacitor [capacitance=10µF package="100 mil [THT, electrolytic]"]
  C1 = Ceramic Capacitor [capacitance=100nF package="1206 [SMD, multilayer]"]
  R3 = Resistor [tolerance=±5% resistance=22k package="0603 [SMD]"]
  R4-Pullup = Resistor [tolerance=±5% resistance=4.7k package="0603 [SMD]"]
  R5-Pullup = Resistor [tolerance=±5% resistance=4.7k package="0603 [SMD]"]

nets (from the schematic view):
  VCC: IC2.OUT, U1.VCC, U1.CH_PD, R1.P$2, IC1.Vref, IC1.Vdd, C3.+, R3.Pin_1, R4-Pullup.Pin_1, R5-Pullup.Pin_1
  GND: IC2.GND, U1.GND, R2.Pin_0, T1.GND, IC1.AIN0, IC1.AIN1, IC1.A0, IC1.A1, IC1.A2, IC1.Vss, IC1.EXT, IC1.AGND
  N1: IC2.IN, C1.1
  N2: U1.GPIO_0, IC1.SDA, R5-Pullup.Pin_0
  N3: U1.GPIO_2, IC1.SCL, R4-Pullup.Pin_0
  N4: R1.P$1, R2.Pin_1, IC1.AIN2
  N5: T1.Out, IC1.AIN3

notes:
  SCL
  SDA

custom parts:
  ESP8266 WiFi Module: Generic WiFi Module based on the ESP8266 with onboard PCB antenna and UART communications
  LM335 Temperature Sensor: A LM35 temperature sensor with a temperature range from -55°C to 150°C.
  DIP - 16 pins: PCF8591 Analog to digital(ADC) with 4 channels and one channel of digital to analog , Communicate by I2C.
